// Digital circuit CPU.dig as structural Verilog
module CPU (
  input  clk,
  input  clk_2,
  input  [31:0] Interface
);

  wire button_1_out, Clk_t, comparator_1_eq, Ctrl_Alloc, Ctrl_AllocOut, Ctrl_BusMux0, Ctrl_BusMux1,
       Ctrl_Dealloc, Ctrl_InterfaceOut, Ctrl_LoadInst, Ctrl_MemAddrIn, Ctrl_MemDataIn, Ctrl_MemDataOut,
       Ctrl_SetFirstBlock, dipswitch_1_out, Hold, mmu_1_p10, mmu_1_p11, multiplexer_2_out, multiplexer_5_out,
       or_2_out, or_3_out, or_4_out, ShadCp_Active, ShadCp_Activen, ShadCpClk;
  wire [1:0] dipswitch_27_out;
  wire [3:0] counter_2_out;
  wire [7:0] Instruction_q;
  wire [28:8] multiplexer_7_out;
  wire [31:0] Address, Boot_Sequencer_d, Bus, Bus_Unmuxed, Bytecode_Executor_d, MemAddrIn_out, MemoryAddr_q,
       mmu_1_p7, mmu_1_p8, multiplexer_3_out, ShadCp_Addr;

  PullDown #(.Bits(32)) pulldown_1 (.out(Bus_Unmuxed));
  Multiplexer #(.Selector_Bits(2), .Bits(32)) multiplexer_1 (
    .sel({Ctrl_BusMux1, Ctrl_BusMux0}), .in_0(Bus_Unmuxed), .in_1({Bus_Unmuxed[23:0], Bus_Unmuxed[31:24]}),
    .in_2({Bus_Unmuxed[15:0], Bus_Unmuxed[31:16]}),
    .in_3({Bus_Unmuxed[7:0], Bus_Unmuxed[31:16], Bus_Unmuxed[7:0]}), .out(Bus));
  PullDown #(.Bits(32)) pulldown_2 (.out(Bus));
  and and_1 (ShadCpClk, clk, ShadCp_Active);
  not not_1 (ShadCp_Active, ShadCp_Activen);
  // MMU mmu_1: pin names not known; wires that end beside it: Ctrl_Alloc, Ctrl_Dealloc, Ctrl_AllocOut, Ctrl_SetFirstBlock, Clk_t, Bus, mmu_1_p7, mmu_1_p8, mmu_1_p7, mmu_1_p10, mmu_1_p11, Hold
  Counter #(.Bits(32)) counter_1 (.en(ShadCp_Active), .C(ShadCpClk), .clr(1'b0), .out(ShadCp_Addr));  // open: ovf
  or or_1 (ShadCp_Activen, ShadCp_Activen, comparator_1_eq);
  Comparator #(.Bits(32)) comparator_1 (.a(ShadCp_Addr), .b(32'h100000), .eq(comparator_1_eq));  // open: gt, lt
  Register #(.Bits(32)) MemoryAddr (.D(Bus), .C(Clk_t), .en(Ctrl_MemAddrIn), .Q(MemoryAddr_q));
  Multiplexer multiplexer_2 (.sel(Hold), .in_0(mmu_1_p10), .in_1(Ctrl_MemDataIn), .out(multiplexer_2_out));
  Multiplexer #(.Bits(32)) multiplexer_3 (.sel(Hold), .in_0(MemoryAddr_q), .in_1(mmu_1_p8), .out(multiplexer_3_out));
  Multiplexer #(.Bits(32)) multiplexer_4 (
    .sel(ShadCp_Activen), .in_0(ShadCp_Addr), .in_1(multiplexer_3_out), .out(Address));
  or or_2 (or_2_out, ShadCp_Active, multiplexer_2_out);
  Multiplexer multiplexer_5 (.sel(Hold), .in_0(mmu_1_p11), .in_1(Ctrl_MemDataOut), .out(multiplexer_5_out));
  or or_3 (or_3_out, ShadCpClk, Clk_t);
  // ROM rom_1: pin names not known; wires that end beside it: Address, ShadCp_Active, mmu_1_p7
  RAM ram_1 (.Addr(Address), .D_In(mmu_1_p7), .Str(or_2_out), .Clk(or_3_out), .Ld(multiplexer_5_out), .D_Out(mmu_1_p7));
  Seven_Seg_Hex seven_seg_hex_1 (.d(Address[31:28]), .dp(1'b0));
  Button button_1 (.out(button_1_out));
  DipSwitch dipswitch_1 (.out(dipswitch_1_out));
  Seven_Seg_Hex seven_seg_hex_2 (.d(Address[27:24]), .dp(1'b0));
  Multiplexer multiplexer_6 (.sel(dipswitch_1_out), .in_0(button_1_out), .in_1(clk_2), .out(Clk_t));
  or or_4 (or_4_out, Ctrl_MemDataOut, ShadCp_Active);
  assign Bus_Unmuxed = or_4_out ? mmu_1_p7 : 32'bz;  // Driver driver_1
  assign mmu_1_p7 = Ctrl_MemDataIn ? Bus : 32'bz;  // Driver driver_2
  Seven_Seg_Hex seven_seg_hex_3 (.d(Address[23:20]), .dp(1'b0));
  Seven_Seg_Hex seven_seg_hex_4 (.d(Address[19:16]), .dp(1'b0));
  Seven_Seg_Hex seven_seg_hex_5 (.d(Address[15:12]), .dp(1'b0));
  Seven_Seg_Hex seven_seg_hex_6 (.d(Address[11:8]), .dp(1'b0));
  Seven_Seg_Hex seven_seg_hex_7 (.d(Address[7:4]), .dp(1'b0));
  Seven_Seg_Hex seven_seg_hex_8 (.d(Address[3:0]), .dp(1'b0));
  Counter #(.Bits(4)) counter_2 (.en(Hold), .C(Clk_t), .clr(1'b0), .out(counter_2_out));  // open: ovf
  Register #(.Bits(8)) Instruction (.D(Bus[7:0]), .C(Clk_t), .en(Ctrl_LoadInst), .Q(Instruction_q));
  Seven_Seg_Hex seven_seg_hex_9 (.d(Bus[31:28]), .dp(1'b0));
  Seven_Seg_Hex seven_seg_hex_10 (.d(Bus[27:24]), .dp(1'b0));
  Seven_Seg_Hex seven_seg_hex_11 (.d(Bus[23:20]), .dp(1'b0));
  ROM #(.AddrBits(4), .Bits(32)) Boot_Sequencer (.A(counter_2_out), .sel(1'b1), .D(Boot_Sequencer_d));
  ROM #(.AddrBits(12), .Bits(32)) Bytecode_Executor (
    .A({Instruction_q, counter_2_out}), .sel(1'b1), .D(Bytecode_Executor_d));
  Seven_Seg_Hex seven_seg_hex_12 (.d(Bus[19:16]), .dp(1'b0));
  DipSwitch MemAddrIn (.out(MemAddrIn_out[0]));
  DipSwitch MemDataIn (.out(MemAddrIn_out[1]));
  DipSwitch MemDataOut (.out(MemAddrIn_out[2]));
  DipSwitch Alloc (.out(MemAddrIn_out[3]));
  DipSwitch Dealloc (.out(MemAddrIn_out[4]));
  DipSwitch SetFirstBlock (.out(MemAddrIn_out[5]));
  DipSwitch AllocOut (.out(MemAddrIn_out[6]));
  DipSwitch LoadInstr (.out(MemAddrIn_out[7]));
  DipSwitch dipswitch_2 (.out(MemAddrIn_out[8]));
  DipSwitch dipswitch_3 (.out(MemAddrIn_out[9]));
  DipSwitch dipswitch_4 (.out(MemAddrIn_out[10]));
  DipSwitch dipswitch_5 (.out(MemAddrIn_out[11]));
  DipSwitch dipswitch_6 (.out(MemAddrIn_out[12]));
  DipSwitch dipswitch_7 (.out(MemAddrIn_out[13]));
  DipSwitch dipswitch_8 (.out(MemAddrIn_out[14]));
  DipSwitch dipswitch_9 (.out(MemAddrIn_out[15]));
  DipSwitch dipswitch_10 (.out(MemAddrIn_out[16]));
  DipSwitch dipswitch_11 (.out(MemAddrIn_out[17]));
  DipSwitch dipswitch_12 (.out(MemAddrIn_out[18]));
  DipSwitch dipswitch_13 (.out(MemAddrIn_out[19]));
  DipSwitch dipswitch_14 (.out(MemAddrIn_out[20]));
  DipSwitch dipswitch_15 (.out(MemAddrIn_out[21]));
  DipSwitch dipswitch_16 (.out(MemAddrIn_out[22]));
  DipSwitch dipswitch_17 (.out(MemAddrIn_out[23]));
  DipSwitch dipswitch_18 (.out(MemAddrIn_out[24]));
  DipSwitch dipswitch_19 (.out(MemAddrIn_out[25]));
  DipSwitch dipswitch_20 (.out(MemAddrIn_out[26]));
  DipSwitch dipswitch_21 (.out(MemAddrIn_out[27]));
  DipSwitch dipswitch_22 (.out(MemAddrIn_out[28]));
  DipSwitch dipswitch_23 (.out(MemAddrIn_out[29]));
  DipSwitch dipswitch_24 (.out(MemAddrIn_out[30]));
  DipSwitch dipswitch_25 (.out(MemAddrIn_out[31]));
  Seven_Seg_Hex seven_seg_hex_13 (.d(Bus[15:12]), .dp(1'b0));
  Seven_Seg_Hex seven_seg_hex_14 (.d(Bus[11:8]), .dp(1'b0));
  DipSwitch dipswitch_26 (.out(dipswitch_27_out[0]));
  DipSwitch dipswitch_27 (.out(dipswitch_27_out[1]));
  Multiplexer #(.Selector_Bits(2), .Bits(32)) multiplexer_7 (
    .sel(dipswitch_27_out), .in_0(Boot_Sequencer_d), .in_1(Bytecode_Executor_d), .in_2(MemAddrIn_out),
    .in_3(MemAddrIn_out),
    .out({Ctrl_InterfaceOut, Ctrl_BusMux1, Ctrl_BusMux0, multiplexer_7_out, Ctrl_LoadInst, Ctrl_AllocOut, Ctrl_SetFirstBlock, Ctrl_Dealloc, Ctrl_Alloc, Ctrl_MemDataOut, Ctrl_MemDataIn, Ctrl_MemAddrIn}));
  assign Bus_Unmuxed = Ctrl_InterfaceOut ? Interface : 32'bz;  // Driver driver_3
  Seven_Seg_Hex seven_seg_hex_15 (.d(Bus[7:4]), .dp(1'b0));
  Seven_Seg_Hex seven_seg_hex_16 (.d(Bus[3:0]), .dp(1'b0));

  // Notes on the sheet:
  //   clk: Hz: 2147483647
  //   clk_2: Hz: 500000
  //   Bus Muxer
  //   ABCD
  //   BCDA
  //   CDAB
  //   DABC
  //   Memory
  //   Memory Address
  //   Control
  //   Bus
  //   Boot_Sequencer loads ucodeBootSeq.bin
endmodule
