// Digital circuit MMU.dig as structural Verilog
module MMU (
  input  Ctrl_Alloc,
  input  Ctrl_Dealloc,
  input  Ctrl_AllocOut,
  input  [31:0] Bus,
  input  [31:0] MemDataIn,
  input  Clk,
  output [31:0] MemAddr,
  output [31:0] MemDataOut,
  output MemStr,
  output MemLd,
  output CPU_Hold
);

  wire comparator_1_eq, comparator_1_gt, or_1_out, Step_ovf;
  wire [7:1] or_2_out;
  wire [23:0] Microcode_d;
  wire [31:0] add_1_s, Available_q, Desired_q, driver_1_out, First_q, Next_q, Previous_q, sub_1_s, Testing_q;

  Register #(.Bits(3)) State (.D(Microcode_d[23:21]), .C(Clk), .en(Microcode_d[20]), .Q(or_2_out[7:5]));
  Counter #(.Bits(3)) Step (.en(1'b1), .C(Clk), .clr(or_1_out), .out(or_2_out[4:2]), .ovf(Step_ovf));
  or or_1 (or_1_out, Microcode_d[19], Step_ovf);
  // Probe on or_2_out[7:5]
  // Probe on or_2_out[4:2]
  ROM #(.bigEndian("true"), .AddrBits(8), .Bits(24)) Microcode (
    .A({or_2_out, Ctrl_Alloc}), .sel(1'b1), .D({Microcode_d[23:17], MemStr, MemLd, Microcode_d[14:0]}));
  // Probe on {Microcode_d[23:17], MemStr, MemLd, Microcode_d[14:0]}
  Register #(.Bits(32)) Available (.D(driver_1_out), .C(Clk), .en(Microcode_d[0]), .Q(Available_q));
  assign driver_1_out = Microcode_d[1] ? Available_q : 32'bz;  // Driver driver_1
  Register #(.Bits(32)) Desired (.D(Bus), .C(Clk), .en(Microcode_d[2]), .Q(Desired_q));
  assign driver_1_out = Microcode_d[3] ? Desired_q : 32'bz;  // Driver driver_2
  Register #(.Bits(32)) register_1 (.D(driver_1_out), .C(Clk), .en(Microcode_d[14]), .Q(MemAddr));
  RS_FF_AS rs_ff_as_1 (.S(Microcode_d[17]), .R(Microcode_d[18]), .Q(CPU_Hold));  // open: nQ
  Comparator #(.Bits(32)) comparator_1 (
    .a(Available_q), .b(Desired_q), .gt(comparator_1_gt), .eq(comparator_1_eq));  // open: lt
  Sub #(.Bits(32)) sub_1 (.a(Available_q), .b(Desired_q), .c_i(1'b0), .s(sub_1_s));  // open: c_o
  assign driver_1_out = MemLd ? MemDataIn : 32'bz;  // Driver driver_3
  assign MemDataOut = MemStr ? driver_1_out : 32'bz;  // Driver driver_4
  or or_2 (or_2_out[1], comparator_1_gt, comparator_1_eq);
  assign driver_1_out = Microcode_d[4] ? sub_1_s : 32'bz;  // Driver driver_5
  Register #(.Bits(32)) First (.D(driver_1_out), .C(Clk), .en(Microcode_d[5]), .Q(First_q));
  Register #(.Bits(32)) Previous (.D(driver_1_out), .C(Clk), .en(Microcode_d[7]), .Q(Previous_q));
  Register #(.Bits(32)) Testing (.D(driver_1_out), .C(Clk), .en(Microcode_d[9]), .Q(Testing_q));
  Register #(.Bits(32)) Next (.D(driver_1_out), .C(Clk), .en(Microcode_d[12]), .Q(Next_q));
  assign driver_1_out = Microcode_d[6] ? First_q : 32'bz;  // Driver driver_6
  assign driver_1_out = Microcode_d[8] ? Previous_q : 32'bz;  // Driver driver_7
  assign driver_1_out = Microcode_d[10] ? Testing_q : 32'bz;  // Driver driver_8
  assign driver_1_out = Microcode_d[11] ? add_1_s : 32'bz;  // Driver driver_9
  assign driver_1_out = Microcode_d[13] ? Next_q : 32'bz;  // Driver driver_10
  Add add_1 (.a(Testing_q[0]), .b(1'b1), .c_i(1'b0), .s(add_1_s[0]));  // open: c_o
  // Pins of 1 and 32 bits meet at Testing_q
  // Pins of 1 and 32 bits meet at add_1_s
  // Pins of 1 and 32 bits meet at 32'h1

  // Notes on the sheet:
  //   Microcode loads MMU-ucode.bin
  //   Sufficient
  //   Remaining
endmodule
